# Fritzing sketch MemoryGame (saved by Fritzing 0.8.7b)
breadboards: 1

parts:
  Part1 = Arduino Uno (Rev3)
  S1 = Pushbutton [package="[THT]"]
  S2 = Pushbutton [package="[THT]"]
  LCD1 = LCD screen
  LED1 = RGB LED (com. anode, rbg) [package="5 mm [THT]"]
  J1 = Piezo Speaker
  R1 = Rotary Potentiometer (Small) [maximum_resistance=100kΩ package=THT]
  R2 = Resistor [tolerance=±5% resistance=220 package=THT]

nets:
  N1: Part1.D8, S1.Pin_1, S1.Pin_2
  N2: Part1.D9_PWM, LED1.common_anode
  N3: Part1.D10_PWM/SS, LED1.red_cathode
  N4: Part1.D11_PWM/MOSI, LCD1.E
  N5: Part1.D12/MISO, LCD1.R/W
  N6: Part1.D13/SCK, J1.pin2
  GND: Part1.GND, S1.Pin_3, S1.Pin_4, S2.Pin_3, S2.Pin_4, LCD1.VSS, LCD1.RS, LCD1.LED-, LED1.blue_cathode, J1.pin1, R1.leg1
  N7: Part1.D2, LCD1.DB7
  N8: Part1.D3_PWM, LCD1.DB6
  N9: Part1.D4, LCD1.DB5
  N10: Part1.D5_PWM, LCD1.DB4
  N11: Part1.D6_PWM, LED1.green_cathode
  N12: Part1.D7, S2.Pin_1, S2.Pin_2
  5V: Part1.5V, LCD1.VDD, R1.leg2, R2.Pin_1
  N13: LCD1.V0, R1.wiper
  N14: LCD1.LED+, R2.Pin_0
